# Fritzing sketch ambientsensorstation (saved by Fritzing 0.9.3b)
breadboards: 1

parts:
  NodeMCU4 = NodeMCU V3.0
  Part1 = Adafruit BME280
  Part2 = Adafruit TSL2561 [part_number="Adafruit #439"]
  Part3 = Adafruit CCS811

nets:
  N1: NodeMCU4.D1, Part2.SCL, Part3.SCL
  N2: NodeMCU4.D2, Part2.SDA, Part3.SDA
  VIN: NodeMCU4.3V3, Part1.VIN, Part2.VIN, Part3.VIN
  GND: NodeMCU4.GND#6, NodeMCU4.GND#13, NodeMCU4.GND#16, NodeMCU4.GND#33, Part1.GND, Part2.GND, Part3.GND, Part3.!WAKE
  N3: NodeMCU4.D5, Part1.SCK/SCL
  N4: NodeMCU4.D6, Part1.SDI/SDA
  N5: NodeMCU4.D7, Part1.CS
  N6: NodeMCU4.D8, Part1.SDO/ADR

custom parts:
  NodeMCU V3.0: ESP8266 based NodeMCU
  Adafruit BME280: Bosch has stepped up their game with their new BME280 sensor, an environmental sensor with temperature, barometric pressure and humidity! This sensor is great for all sorts of weather/environmental sensing and can even be used in both I2C and SPI! This precision sensor from Bosch is the best low-cost sensing solution for measuring humidity with ±3% accuracy, barometric pressure with ±1 hPa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
  Adafruit TSL2561: The TSL2561 luminosity sensor is an advanced digital light sensor, ideal for use in a wide range of light situations. Compared to low cost CdS cells, this sensor is more precise, allowing for exact lux calculations and can be configured for different gain/timing ranges to detect light ranges from up to 0.1 - 40,000+ Lux on the fly. The best part of this sensor is that it contains both infrared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
